// Logisim project TP.circ as structural Verilog: 6 circuits, main circuit main
module main (
  input  in_1
);

  wire banc_reg_1_p2, banc_reg_1_p8, clock_1_out, clock_2_out, decodeur_1_imm_reg;
  wire [1:0] decodeur_1_op;
  wire [3:0] decodeur_1_rd, decodeur_1_rot, decodeur_1_rs1, decodeur_1_rs2;
  wire [7:0] decodeur_1_imm;
  wire [31:0] adder_1_out, banc_reg_1_p9, calculateur_immediat_1_out_3, multiplexer_1_out, PC_q, ram_1_dout;

  Register #(.width(32)) PC (.D(adder_1_out), .en(1'b1), .clk(clock_1_out), .Q(PC_q));  // open: clr
  Clock clock_1 (.out(clock_1_out));
  RAM #(.addrWidth(24), .asyncread("true"), .dataWidth(32)) ram_1 (
    .addr(PC_q[25:2]), .oe(1'b1), .dout(ram_1_dout));  // open: we, clk, din
  Adder #(.width(32)) adder_1 (.a(PC_q), .b(32'h4), .out(adder_1_out));  // open: cin, cout
  // Probe on ram_1_dout
  // Probe on {{8{1'b0}}, PC_q[23:0]}
  decodeur decodeur_1 (
    .in_1(ram_1_dout), .Rd(decodeur_1_rd), .Rs1(decodeur_1_rs1), .Rs2(decodeur_1_rs2), .Op(decodeur_1_op),
    .Imm_reg(decodeur_1_imm_reg), .Imm(decodeur_1_imm), .Rot(decodeur_1_rot));
  calculateur_immediat calculateur_immediat_1 (
    .Imm(decodeur_1_imm), .Rot(decodeur_1_rot), .out_3(calculateur_immediat_1_out_3));
  // Probe on decodeur_1_rs1
  // Probe on decodeur_1_rs2
  // Probe on decodeur_1_rd
  Clock clock_2 (.out(clock_2_out));
  // Probe on calculateur_immediat_1_out_3
  // banc_reg banc_reg_1: pin names not known; wires that end beside it: clock_2_out, banc_reg_1_p2, decodeur_1_rs1, decodeur_1_rs2, decodeur_1_rd, in_1, {{8{1'b0}}, PC_q[23:0]}, banc_reg_1_p8, banc_reg_1_p9
  // Probe on banc_reg_1_p9
  Multiplexer #(.width(32)) multiplexer_1 (
    .in0(banc_reg_1_p9), .in1(calculateur_immediat_1_out_3), .out(multiplexer_1_out), .sel(decodeur_1_imm_reg));
  // Probe on multiplexer_1_out
  // ALU alu_1: pin names not known; wires that end beside it: banc_reg_1_p8, multiplexer_1_out, decodeur_1_op, banc_reg_1_p2
  // Probe on banc_reg_1_p2
endmodule

module decodeur (
  input  [31:0] in_1,
  output [3:0] Rd,
  output [3:0] Rs1,
  output [3:0] Rs2,
  output [1:0] Op,
  output Imm_reg,
  output [7:0] Imm,
  output [3:0] Rot
);

  wire and_1_out, not_1_out;

  not not_1 (not_1_out, in_1[24]);
  and and_1 (and_1_out, in_1[23], not_1_out);
  or or_1 (Op[0], in_1[21], in_1[22]);
  or or_2 (Op[1], in_1[22], and_1_out);

  assign Imm = in_1[7:0];
  assign Imm_reg = in_1[25];
  assign Rd = in_1[15:12];
  assign Rot = in_1[11:8];
  assign Rs1 = in_1[19:16];
  assign Rs2 = in_1[3:0];
endmodule

module calculateur_immediat (
  input  [7:0] Imm,
  input  [3:0] Rot,
  output [31:0] out_3
);

  Shifter #(.shift("rr"), .width(32)) shifter_1 (.in({{25{Imm[7]}}, Imm[6:0]}), .\dist ({Rot, 1'b0}), .out(out_3));
endmodule

module gestion_cond (
  input  [3:0] Cond,
  input  [3:0] NZCV,
  input  MaJ,
  output Exec
);

  wire and_1_out, and_2_out, and_3_out, and_4_out, and_5_out, and_6_out, and_7_out, and_8_out,
       decodeur_cond_1_cc_lo, decodeur_cond_1_cs_hs, decodeur_cond_1_eq, decodeur_cond_1_mi,
       decodeur_cond_1_ne, decodeur_cond_1_pl, decodeur_cond_1_vc, decodeur_cond_1_vs, not_1_out, not_2_out,
       not_3_out, not_4_out, repartiteur_nzcv_1_c, repartiteur_nzcv_1_n, repartiteur_nzcv_1_v,
       repartiteur_nzcv_1_z;

  decodeur_cond decodeur_cond_1 (
    .Cond(Cond), .EQ(decodeur_cond_1_eq), .NE(decodeur_cond_1_ne), .CS_HS(decodeur_cond_1_cs_hs),
    .CC_LO(decodeur_cond_1_cc_lo), .MI(decodeur_cond_1_mi), .PL(decodeur_cond_1_pl), .VS(decodeur_cond_1_vs),
    .VC(decodeur_cond_1_vc));  // open: HI, LS, GE, LT, GT, LE, AL, NV
  repartiteur_NZCV repartiteur_nzcv_1 (
    .NZCV(NZCV), .N(repartiteur_nzcv_1_n), .Z(repartiteur_nzcv_1_z), .C(repartiteur_nzcv_1_c),
    .V(repartiteur_nzcv_1_v));
  and and_1 (and_1_out, decodeur_cond_1_eq, repartiteur_nzcv_1_z);
  and and_2 (and_2_out, decodeur_cond_1_ne, not_1_out);
  not not_1 (not_1_out, repartiteur_nzcv_1_z);
  and and_3 (and_3_out, decodeur_cond_1_cs_hs, repartiteur_nzcv_1_c);
  and and_4 (and_4_out, decodeur_cond_1_cc_lo, not_2_out);
  not not_2 (not_2_out, repartiteur_nzcv_1_c);
  and and_5 (and_5_out, decodeur_cond_1_mi, repartiteur_nzcv_1_n);
  and and_6 (and_6_out, decodeur_cond_1_pl, not_3_out);
  not not_3 (not_3_out, repartiteur_nzcv_1_n);
  and and_7 (and_7_out, decodeur_cond_1_vs, repartiteur_nzcv_1_v);
  not not_4 (not_4_out, repartiteur_nzcv_1_v);
  and and_8 (and_8_out, decodeur_cond_1_vc, not_4_out);
  or or_1 (Exec, and_1_out, and_2_out, and_3_out, and_4_out, and_5_out, and_6_out, and_7_out, and_8_out);
endmodule

module decodeur_cond (
  input  [3:0] Cond,
  output EQ,
  output NE,
  output CS_HS,
  output CC_LO,
  output MI,
  output PL,
  output VS,
  output VC,
  output HI,
  output LS,
  output GE,
  output LT,
  output GT,
  output LE,
  output AL,
  output NV
);

  Decoder #(.select(4)) decoder_1 (
    .out0(EQ), .out1(NE), .out2(CS_HS), .out3(CC_LO), .out4(MI), .out5(PL), .out6(VS), .out7(VC), .out8(HI),
    .out9(LS), .out10(GE), .out11(LT), .out12(GT), .out13(LE), .out14(AL), .out15(NV), .sel(Cond));  // open: en
endmodule

module repartiteur_NZCV (
  input  [3:0] NZCV,
  output N,
  output Z,
  output C,
  output V
);


  assign C = NZCV[1];
  assign N = NZCV[3];
  assign V = NZCV[0];
  assign Z = NZCV[2];
endmodule
